# Fritzing sketch RFID_OS_Login_ArduinoMicro (saved by Fritzing 0.9.3b)

parts:
  Parça1 = Arduino Micro (Rev3)
  Part4 = RFID-RC522 [part_number=101218]
  LED1 = LED - 5mm [color="Red (633nm)" package="5 mm [THT]"]
  LED2 = LED - 5mm [color="Green (555nm)" package="5 mm [THT]"]
  R1 = Resistor [tolerance=±5% resistance=220 package=THT]

nets:
  N1: Parça1.MOSI, Part4.MOSI
  GND: Parça1.GND, Part4.GND, R1.Pin_1
  N2: Parça1.D2/SDA, Part4.SDA
  N3: Parça1.D3/SCL, Part4.RST
  N4: Parça1.D7, LED1.anode
  N5: Parça1.D8_PWM/A8, LED2.anode
  N6: Parça1.SCK, Part4.SCK
  N7: Parça1.MISO, Part4.MISO
  3V3: Parça1.3V3, Part4.3.3V
  N8: LED1.cathode, LED2.cathode, R1.Pin_0
