# Fritzing sketch RFID_OS_Login_ProMicro (saved by Fritzing 0.9.3b)

parts:
  Pro_Micro = Pro Micro
  Part5 = RFID-RC522 [part_number=101218]

nets:
  GND: Pro_Micro.GND, Part5.GND
  N1: Pro_Micro.D5, Part5.RST
  N2: Pro_Micro.D7, Part5.SDA
  N3: Pro_Micro.D16/MOSI, Part5.MOSI
  N4: Pro_Micro.D14/MISO, Part5.MISO
  N5: Pro_Micro.D15/SCLK, Part5.SCK
  VCC: Pro_Micro.VCC, Part5.3.3V

custom parts:
  Pro Micro: The SparkFun Pro Micro is a complete USB-based microcontoller development system, in a very small footprint, capable of implementing many types of projects. All programming can be done via the USB port.
